// Logisim project Digital_Error_Detection_System_Wired.circ as structural Verilog: 1 circuit, main circuit main
module main (
  input  ERROR,
  input  NO_ERROR,
  output D0,
  output D1,
  output D2,
  output D3,
  output F0,
  output F1,
  output F2,
  output F3,
  output Fp
);

  wire xor_1_p3, xor_2_p3, xor_3_p3, xor_4_p4, xor_5_p5, xor_6_p5, xor_7_p5, xor_8_p5, xor_9_p3, xor_10_p3,
       xor_11_p3;

  // XOR_Gate xor_1: pin names not known; wires that end beside it: D0, D1, xor_1_p3
  // XOR_Gate xor_2: pin names not known; wires that end beside it: xor_1_p3, D2, xor_2_p3
  // XOR_Gate xor_3: pin names not known; wires that end beside it: xor_2_p3, D3, xor_3_p3
  // XOR_Gate xor_4: pin names not known; wires that end beside it: D0, F0, D1, xor_4_p4
  // XOR_Gate xor_5: pin names not known; wires that end beside it: F0, D1, F1, D2, xor_5_p5
  // XOR_Gate xor_6: pin names not known; wires that end beside it: F1, D2, F2, D3, xor_6_p5
  // XOR_Gate xor_7: pin names not known; wires that end beside it: F2, D3, F3, xor_3_p3, xor_7_p5
  // XOR_Gate xor_8: pin names not known; wires that end beside it: Fp, Fp, F3, xor_3_p3, xor_8_p5
  // XOR_Gate xor_9: pin names not known; wires that end beside it: xor_4_p4, xor_5_p5, xor_9_p3
  // XOR_Gate xor_10: pin names not known; wires that end beside it: xor_6_p5, xor_9_p3, xor_10_p3
  // XOR_Gate xor_11: pin names not known; wires that end beside it: xor_7_p5, xor_10_p3, xor_11_p3
  // XOR_Gate xor_12: pin names not known; wires that end beside it: xor_8_p5, xor_11_p3, ERROR
  // NOT_Gate not_1: pin names not known; wires that end beside it: ERROR, NO_ERROR
endmodule
