// Logisim project ErrorDetection.circ as structural Verilog: 1 circuit, main circuit main
module main (
  input  D7,
  input  D6,
  input  D5,
  input  D4,
  input  D3,
  input  D2,
  input  D1,
  input  D0,
  input  R7,
  input  R6,
  input  R5,
  input  R4,
  input  R3,
  input  R2,
  input  R1,
  input  R0,
  input  RC2,
  input  RC1,
  input  RC0,
  output C2,
  output C0,
  output C1,
  output S2,
  output ERROR,
  output S0,
  output S1
);

  wire undriven, undriven_2, xor_9_out, xor_10_p1, xor_10_p5, xor_11_out, xor_12_out, xor_13_out, xor_14_out,
       xor_15_out, xor_16_out, xor_17_out, xor_18_out, xor_22_out, xor_23_out;

  // XOR_Gate xor_1 has open pins: in0=D6, in1=D3, out=open
  // XOR_Gate xor_2 has open pins: in0=D2, in1=D1, out=open
  // XOR_Gate xor_3 has open pins: in0=D7, in1=D4, out=open
  // XOR_Gate xor_4 has open pins: in0=D7, in1=D5, out=open
  // XOR_Gate xor_5 has open pins: in0=R6, in1=R3, out=open
  // XOR_Gate xor_6: pin names not known; wires that end beside it: R7
  // XOR_Gate xor_7: pin names not known; wires that end beside it: R7
  xor xor_8 (C2, undriven, undriven_2);
  xor xor_9 (xor_9_out, D3, D2);
  // XOR_Gate xor_10: pin names not known; wires that end beside it: xor_10_p1, D3, xor_10_p1, D2, xor_10_p5
  // XOR_Gate xor_11 has open pins: out=xor_11_out
  buf xor_12 (xor_12_out, R4);  // XOR_Gate
  xor xor_13 (xor_13_out, R2, R5);
  buf xor_14 (xor_14_out, D0);  // XOR_Gate
  // XOR_Gate xor_15 has open pins: out=xor_15_out
  buf xor_16 (xor_16_out, R1);  // XOR_Gate
  // XOR_Gate xor_17 has open pins: out=xor_17_out
  xor xor_18 (xor_18_out, R1, R0);
  // XOR_Gate xor_19 has open pins: out=C0
  buf xor_20 (C1, D0);  // XOR_Gate
  buf xor_21 (S2, RC2);  // XOR_Gate
  buf xor_22 (xor_22_out, R0);  // XOR_Gate
  buf xor_23 (xor_23_out, RC1);  // XOR_Gate
  buf xor_24 (S0, RC0);  // XOR_Gate
  // XOR_Gate xor_25 has open pins: out=S1
  // OR_Gate or_1: pin names not known; wires that end beside it: S2, S1
  // OR_Gate or_2 has open pins: out=ERROR

  // Notes on the sheet:
  //   TRANSMITTER / CRC ENCODER
  //   RECEIVER / CRC CHECKER
  //   DIGITAL DATA TRANSMISSION ERROR DETECTION SYSTEM
  //   Generator: G(x) = x^3 + x + 1
  //   Valid codeword -> S2=S1=S0=0; otherwise ERROR=1
  //   Demo: set transmitter data, read C2 C1 C0, then enter the resulting codeword on R7..R0/RC2..RC0. Flip one receiver bit to assert ERROR.
endmodule
