// Logisim project Final project.circ as structural Verilog: 1 circuit, main circuit main
module main (
  input  A,
  input  B,
  input  C,
  input  D,
  output P,
  output out_6,
  output out_7,
  output out_8,
  output out_9
);

  wire xor_1_out, xor_2_out;

  xor xor_1 (xor_1_out, A, B);
  xor xor_2 (xor_2_out, xor_1_out, C);
  xor xor_3 (P, xor_2_out, D);

  assign out_6 = D;
  assign out_7 = C;
  assign out_8 = B;
  assign out_9 = A;

  // Notes on the sheet:
  //   Input
  //   Data
  //   Bits
  //   (Parity Bit)
endmodule
