// Logisim project error_detection.circ as structural Verilog: 1 circuit, main circuit main
module main (
  input  D7,
  input  R7,
  input  D6,
  input  R6,
  input  D5,
  input  R5,
  input  RC2,
  input  D4,
  input  R4,
  input  RC1,
  input  D3,
  input  R3,
  input  RC0,
  input  D2,
  input  R2,
  input  D1,
  input  R1,
  input  D0,
  input  R0,
  output C2,
  output C1,
  output C0,
  output S2,
  output S1,
  output S0,
  output ERROR
);

  wire xor_1_p4, xor_1_p5, xor_2_p7, xor_4_p6, xor_4_p7, xor_5_p10, xor_7_p7, xor_8_p9, xor_12_p4, xor_12_p5,
       xor_13_p7, xor_15_p10, xor_15_p11, xor_16_p13, xor_18_p10, xor_18_p11, xor_19_p13, xor_21_p10,
       xor_21_p11, xor_22_p13, xor_23_p10, xor_23_p11, xor_26_p3;

  // XOR_Gate xor_1: pin names not known; wires that end beside it: D6, D3, D7, xor_1_p4, xor_1_p5
  // XOR_Gate xor_2: pin names not known; wires that end beside it: D3, D7, D5, D7, xor_1_p4, xor_1_p5, xor_2_p7
  // XOR_Gate xor_3: pin names not known; wires that end beside it: D5, D7, D4, xor_1_p5, xor_2_p7
  // XOR_Gate xor_4: pin names not known; wires that end beside it: xor_1_p4, xor_1_p5, xor_1_p4, D2, xor_1_p5, xor_4_p6, xor_4_p7
  // XOR_Gate xor_5: pin names not known; wires that end beside it: xor_1_p4, xor_1_p5, xor_2_p7, D2, xor_1_p5, D2, xor_2_p7, xor_4_p6, xor_4_p7, xor_5_p10
  // XOR_Gate xor_6: pin names not known; wires that end beside it: xor_1_p5, xor_2_p7, D2, xor_2_p7, D3, xor_4_p7, xor_5_p10
  // XOR_Gate xor_7: pin names not known; wires that end beside it: xor_4_p6, xor_4_p7, xor_4_p6, D1, xor_4_p7, C2, xor_7_p7
  // XOR_Gate xor_8: pin names not known; wires that end beside it: xor_4_p7, xor_5_p10, D1, xor_4_p7, D1, xor_5_p10, C2, xor_7_p7, xor_8_p9
  // XOR_Gate xor_9: pin names not known; wires that end beside it: xor_5_p10, D1, xor_5_p10, D2, xor_7_p7, xor_8_p9
  // XOR_Gate xor_10: pin names not known; wires that end beside it: xor_7_p7, xor_8_p9, xor_7_p7, D0, xor_8_p9, C1, C0
  // XOR_Gate xor_11: pin names not known; wires that end beside it: xor_8_p9, D0, xor_8_p9, D0, C1, C0
  // XOR_Gate xor_12: pin names not known; wires that end beside it: R6, R3, R7, xor_12_p4, xor_12_p5
  // XOR_Gate xor_13: pin names not known; wires that end beside it: R3, R7, R5, R7, xor_12_p4, xor_12_p5, xor_13_p7
  // XOR_Gate xor_14: pin names not known; wires that end beside it: R5, R7, R4, xor_12_p5, xor_13_p7
  // XOR_Gate xor_15: pin names not known; wires that end beside it: R6, R3, R7, R5, xor_12_p4, xor_12_p5, xor_12_p4, R2, xor_12_p5, xor_15_p10, xor_15_p11
  // XOR_Gate xor_16: pin names not known; wires that end beside it: R7, R5, R7, R4, xor_12_p5, xor_13_p7, R2, xor_12_p5, R2, xor_13_p7, xor_15_p10, xor_15_p11, xor_16_p13
  // XOR_Gate xor_17: pin names not known; wires that end beside it: R7, R4, xor_13_p7, R2, xor_13_p7, R3, xor_15_p11, xor_16_p13
  // XOR_Gate xor_18: pin names not known; wires that end beside it: xor_12_p4, R2, xor_12_p5, R2, xor_15_p10, xor_15_p11, xor_15_p10, R1, xor_15_p11, xor_18_p10, xor_18_p11
  // XOR_Gate xor_19: pin names not known; wires that end beside it: xor_12_p5, R2, xor_13_p7, R3, xor_15_p11, xor_16_p13, R1, xor_15_p11, R1, xor_16_p13, xor_18_p10, xor_18_p11, xor_19_p13
  // XOR_Gate xor_20: pin names not known; wires that end beside it: xor_13_p7, R3, xor_16_p13, R1, xor_16_p13, R2, xor_18_p11, xor_19_p13
  // XOR_Gate xor_21: pin names not known; wires that end beside it: xor_15_p10, R1, xor_15_p11, R1, xor_18_p10, xor_18_p11, xor_18_p10, RC2, xor_18_p11, xor_21_p10, xor_21_p11
  // XOR_Gate xor_22: pin names not known; wires that end beside it: xor_15_p11, R1, xor_16_p13, R2, xor_18_p11, xor_19_p13, RC2, xor_18_p11, R0, xor_19_p13, xor_21_p10, xor_21_p11, xor_22_p13
  // XOR_Gate xor_23: pin names not known; wires that end beside it: xor_18_p11, R0, xor_19_p13, R0, xor_21_p11, xor_22_p13, xor_21_p11, RC1, xor_22_p13, xor_23_p10, xor_23_p11, xor_23_p10
  // XOR_Gate xor_24: pin names not known; wires that end beside it: xor_16_p13, R2, xor_19_p13, R0, xor_19_p13, R0, xor_21_p11, xor_22_p13
  // XOR_Gate xor_25: pin names not known; wires that end beside it: xor_19_p13, R0, xor_22_p13, RC1, xor_22_p13, RC0, xor_23_p11, xor_23_p10
  // XOR_Gate xor_26: pin names not known; wires that end beside it: S2, S1, xor_26_p3
  // XOR_Gate xor_27: pin names not known; wires that end beside it: xor_26_p3, xor_26_p3, S0, ERROR

  // Notes on the sheet:
  //   DIGITAL DATA TRANSMISSION ERROR DETECTION SYSTEM
  //   CRC-style error detection using G(x) = x³ + x + 1
  //   TRANSMITTER / ENCODER
  //   Payload D[7:0]
  //   DEMO
  //   Example: data 10110110  → CRC 011  → codeword 10110110011
  //   Flip one received bit (for example R4) and ERROR should assert.
  //   XOR network
  //   CRC bits
  //   Apply any received codeword to R7..R0 + RC2..RC0. For a valid codeword, S2=S1=S0=0.
  //   RECEIVER / CHECKER
  //   ERROR = 1 when the received 11-bit codeword has a non-zero CRC remainder
endmodule
